# Fritzing sketch schematics (saved by Fritzing 0.9.3b)
breadboards: 1

parts:
  Composant1 = Arduino Mega 2560 (Rev3)
  IC1 = IC, DIP package, 28 pins [chip_label="Toshiba TC5565A*L"]

nets:
  N1: Composant1.5V, IC1.pin28
  N2: Composant1.D22, IC1.pin11
  N3: Composant1.D23, IC1.pin12
  N4: Composant1.D24, IC1.pin13
  N5: Composant1.D25, IC1.pin15
  N6: Composant1.D26, IC1.pin16
  N7: Composant1.D27, IC1.pin17
  N8: Composant1.D28, IC1.pin18
  N9: Composant1.D29, IC1.pin19
  N10: Composant1.D30, IC1.pin3
  N11: Composant1.D31, IC1.pin4
  N12: Composant1.D32, IC1.pin5
  N13: Composant1.D33, IC1.pin6
  N14: Composant1.D34, IC1.pin7
  N15: Composant1.D35, IC1.pin8
  N16: Composant1.D36, IC1.pin9
  N17: Composant1.D37, IC1.pin10
  N18: Composant1.D45, IC1.pin2
  N19: Composant1.D46, IC1.pin23
  N20: Composant1.D47, IC1.pin21
  N21: Composant1.D48, IC1.pin24
  N22: Composant1.D49, IC1.pin25
  N23: Composant1.D50, IC1.pin22
  N24: Composant1.D51, IC1.pin20
  N25: Composant1.D52, IC1.pin26
  N26: Composant1.D53, IC1.pin27
  N27: Composant1.GND, IC1.pin14

notes:
  address bus
  data bus
  control
